// Logisim project exam pra problem.circ as structural Verilog: 9 circuits, main circuit main
module main (
  input  a,
  input  b,
  input  c,
  input  d,
  output w,
  output x,
  output y,
  output z
);

  wire and_1_out, and_2_out, not_1_out, xor_1_out;

  xor xor_1 (xor_1_out, b, a);
  not not_1 (not_1_out, c);
  and and_1 (and_1_out, not_1_out, b);
  and and_2 (and_2_out, c, xor_1_out);
  and and_3 (w, a, b, c);
  or or_1 (x, and_1_out, and_2_out);
  xor xor_2 (y, a, c);

  assign z = d;
endmodule

module _2 (
  input  j,
  input  k
);

  wire and_1_out, and_2_out, clock_1_out, d_ff_1_q, d_ff_1_qn, not_1_out, or_1_out;

  and and_1 (and_1_out, j, d_ff_1_qn);
  not not_1 (not_1_out, k);
  and and_2 (and_2_out, not_1_out, d_ff_1_q);
  Clock clock_1 (.out(clock_1_out));
  or or_1 (or_1_out, and_1_out, and_2_out);
  D_Flip_Flop d_ff_1 (.clk(clock_1_out), .D(or_1_out), .Q(d_ff_1_q), .Qn(d_ff_1_qn), .en(1'b1));  // open: preset, reset
endmodule

module _3 (
  input  a1,
  input  a0,
  input  b1,
  input  b0,
  output c0,
  output c1,
  output c2,
  output c3
);

  wire and_1_out, and_2_out, and_3_out, half_adder_1_c;

  and and_1 (and_1_out, b1, a1);
  and and_2 (and_2_out, b1, a0);
  and and_3 (and_3_out, a1, b0);
  and and_4 (c0, b0, a0);
  half_adder half_adder_1 (.x(and_2_out), .y(and_3_out), .s(c1), .c(half_adder_1_c));
  half_adder half_adder_2 (.x(half_adder_1_c), .y(and_1_out), .s(c2), .c(c3));
endmodule

module half_adder (
  input  x,
  input  y,
  output s,
  output c
);

  xor xor_1 (s, x, y);
  and and_1 (c, x, y);
endmodule

module _4 (
);

  wire and_1_out, clock_1_out, j_k_ff_1_q, j_k_ff_2_q, j_k_ff_3_q, j_k_ff_4_q;

  Clock clock_1 (.out(clock_1_out));
  J_K_Flip_Flop #(.trigger("falling")) j_k_ff_1 (
    .J(1'b1), .clk(clock_1_out), .K(1'b1), .Q(j_k_ff_1_q), .en(1'b1), .reset(and_1_out));  // open: Qn, preset
  J_K_Flip_Flop #(.trigger("falling")) j_k_ff_2 (
    .J(1'b1), .clk(j_k_ff_1_q), .K(1'b1), .Q(j_k_ff_2_q), .en(1'b1), .reset(and_1_out));  // open: Qn, preset
  J_K_Flip_Flop #(.trigger("falling")) j_k_ff_3 (
    .J(1'b1), .clk(j_k_ff_2_q), .K(1'b1), .Q(j_k_ff_3_q), .en(1'b1), .reset(and_1_out));  // open: Qn, preset
  and and_1 (and_1_out, j_k_ff_4_q, j_k_ff_2_q);
  J_K_Flip_Flop #(.trigger("falling")) j_k_ff_4 (
    .J(1'b1), .clk(j_k_ff_3_q), .K(1'b1), .Q(j_k_ff_4_q), .en(1'b1), .reset(and_1_out));  // open: Qn, preset
endmodule

module _5 (
  input  a,
  input  b,
  input  c,
  input  d,
  output out_5,
  output out_6,
  output out_7,
  output out_8
);

  wire not_1_out, not_2_out, not_3_out;

  not not_1 (not_1_out, a);
  not not_2 (not_2_out, b);
  not not_3 (not_3_out, c);
  and and_1 (out_5, not_1_out, not_2_out, not_3_out);
  xor xor_1 (out_6, c, b);
  not not_4 (out_8, d);

  assign out_7 = c;
endmodule

module _6 (
);

  wire and_1_out, and_2_out, clock_1_out, j_k_ff_1_q, j_k_ff_2_q, j_k_ff_3_q, j_k_ff_3_qn, or_1_out;

  Clock clock_1 (.out(clock_1_out));
  J_K_Flip_Flop #(.trigger("falling")) j_k_ff_1 (
    .J(1'b1), .clk(clock_1_out), .K(1'b1), .Q(j_k_ff_1_q), .en(1'b1), .reset(or_1_out));  // open: Qn, preset
  J_K_Flip_Flop #(.trigger("falling")) j_k_ff_2 (
    .J(1'b1), .clk(j_k_ff_1_q), .K(1'b1), .Q(j_k_ff_2_q), .en(1'b1), .reset(or_1_out));  // open: Qn, preset
  J_K_Flip_Flop #(.trigger("falling")) j_k_ff_3 (
    .J(1'b1), .clk(j_k_ff_2_q), .K(1'b1), .Q(j_k_ff_3_q), .Qn(j_k_ff_3_qn), .en(1'b1));  // open: preset, reset
  and and_1 (and_1_out, j_k_ff_3_qn, j_k_ff_2_q, j_k_ff_1_q);
  and and_2 (and_2_out, j_k_ff_3_q, j_k_ff_2_q, j_k_ff_1_q);
  or or_1 (or_1_out, and_2_out, and_1_out);
endmodule

module _7 (
);

  wire clock_1_out, j_k_ff_1_q, j_k_ff_1_qn, j_k_ff_2_q, j_k_ff_2_qn;

  Clock clock_1 (.out(clock_1_out));
  J_K_Flip_Flop #(.trigger("falling")) j_k_ff_1 (
    .J(j_k_ff_2_q), .clk(clock_1_out), .K(j_k_ff_2_qn), .Q(j_k_ff_1_q), .Qn(j_k_ff_1_qn), .en(1'b1));  // open: preset, reset
  J_K_Flip_Flop #(.trigger("falling")) j_k_ff_2 (
    .J(j_k_ff_1_qn), .clk(clock_1_out), .K(j_k_ff_1_q), .Q(j_k_ff_2_q), .Qn(j_k_ff_2_qn), .en(1'b1));  // open: preset, reset
endmodule

module _8 (
);

  wire clock_1_out, j_k_ff_1_q, j_k_ff_2_q, j_k_ff_3_q, not_1_out;

  not not_1 (not_1_out, 1'b1);
  Clock clock_1 (.out(clock_1_out));
  J_K_Flip_Flop j_k_ff_1 (
    .J(not_1_out), .clk(clock_1_out), .K(not_1_out), .Q(j_k_ff_1_q), .en(1'b1));  // open: Qn, preset, reset
  J_K_Flip_Flop j_k_ff_2 (.J(1'b1), .clk(clock_1_out), .K(1'b1), .Q(j_k_ff_2_q), .en(1'b1));  // open: Qn, preset, reset
  J_K_Flip_Flop j_k_ff_3 (
    .J(j_k_ff_2_q), .clk(clock_1_out), .K(j_k_ff_2_q), .Q(j_k_ff_3_q), .en(1'b1));  // open: Qn, preset, reset
endmodule
