// Logisim project 1.circ as structural Verilog: 1 circuit, main circuit main
module main (
  input  b,
  input  a,
  output y1,
  output y2
);

  and and_1 (y1, b, a);
  or or_1 (y2, b, a);
endmodule
