// Logisim project 1aa.circ as structural Verilog
module main (
  input  a,
  input  b,
  input  c,
  input  d,
  output out_5
);

  wire nand_1_out, nand_2_out, nand_3_out, not_1_out, not_2_out, not_3_out;

  not not_1 (not_1_out, c);
  not not_2 (not_2_out, d);
  not not_3 (not_3_out, a);
  nand nand_1 (nand_1_out, not_1_out, not_2_out);
  nand nand_2 (nand_2_out, d, b);
  nand nand_3 (nand_3_out, d, c, not_3_out);
  nand nand_4 (out_5, nand_1_out, nand_2_out, nand_3_out);
endmodule
