// Logisim project 2a (1).circ as structural Verilog: 1 circuit, main circuit main
module main (
  input  a,
  input  c,
  input  b,
  input  d,
  output out_5
);

  wire not_1_out, not_2_out, or_1_out, or_2_out;

  not not_1 (not_1_out, b);
  not not_2 (not_2_out, d);
  or or_1 (or_1_out, not_1_out, not_2_out);
  or or_2 (or_2_out, b, d);
  and and_1 (out_5, or_1_out, or_2_out);
endmodule
