// Logisim project 2a.circ as structural Verilog: 1 circuit, main circuit main
module main (
  input  a,
  input  b,
  input  c,
  input  d,
  output out_5
);

  wire and_1_out, and_2_out, and_3_out, and_4_out, and_5_out, and_6_out, not_1_out, not_2_out, not_3_out,
       not_4_out, not_5_out, not_6_out, not_7_out, not_8_out, not_9_out;

  not not_1 (not_1_out, b);
  not not_2 (not_2_out, d);
  not not_3 (not_3_out, a);
  not not_4 (not_4_out, b);
  and and_1 (and_1_out, not_3_out, not_4_out, c, d);
  not not_5 (not_5_out, a);
  and and_2 (and_2_out, not_5_out, b, c, d);
  and and_3 (and_3_out, a, not_1_out, not_6_out, not_2_out);
  not not_6 (not_6_out, c);
  not not_7 (not_7_out, b);
  and and_4 (and_4_out, a, not_7_out, not_8_out, d);
  not not_8 (not_8_out, c);
  not not_9 (not_9_out, b);
  and and_5 (and_5_out, a, not_9_out, c, d);
  and and_6 (and_6_out, a, b, c, d);
  or or_1 (out_5, and_3_out, and_1_out, and_2_out, and_4_out, and_5_out, and_6_out);
endmodule
