// Logisim project 2aa.circ as structural Verilog: 1 circuit, main circuit main
module main (
  input  a,
  input  c,
  input  b,
  input  d,
  output out_5
);

  wire nor_1_out, nor_2_out, not_1_out, not_2_out;

  not not_1 (not_1_out, b);
  not not_2 (not_2_out, d);
  nor nor_1 (nor_1_out, not_1_out, not_2_out);
  nor nor_2 (nor_2_out, b, d);
  nor nor_3 (out_5, nor_1_out, nor_2_out);
endmodule
