// Logisim project 2b.circ as structural Verilog: 1 circuit, main circuit main
module main (
  input  a,
  input  b,
  input  c,
  input  d,
  output out_5
);

  wire not_1_out, not_2_out, not_3_out, not_4_out, not_5_out, or_1_out, or_2_out, or_3_out, or_4_out,
       or_5_out;

  not not_1 (not_1_out, a);
  not not_2 (not_2_out, b);
  not not_3 (not_3_out, d);
  not not_4 (not_4_out, c);
  not not_5 (not_5_out, d);
  or or_1 (or_1_out, d, b);
  or or_2 (or_2_out, not_1_out, not_2_out);
  or or_3 (or_3_out, c, d);
  or or_4 (or_4_out, c, b, not_3_out);
  or or_5 (or_5_out, a, not_4_out, not_5_out);
  or or_6 (out_5, or_1_out, or_2_out, or_3_out, or_4_out, or_5_out);
endmodule
