// Logisim project 2bb.circ as structural Verilog: 1 circuit, main circuit main
module main (
  input  a,
  input  b,
  input  c,
  input  d,
  output out_5
);

  wire nor_1_out, nor_2_out, nor_3_out, nor_4_out, nor_5_out, not_1_out, not_2_out, not_3_out, not_4_out,
       not_5_out;

  not not_1 (not_1_out, a);
  not not_2 (not_2_out, b);
  not not_3 (not_3_out, d);
  not not_4 (not_4_out, c);
  not not_5 (not_5_out, d);
  nor nor_1 (nor_1_out, not_1_out, not_2_out);
  nor nor_2 (nor_2_out, c, d);
  nor nor_3 (nor_3_out, c, b, not_3_out);
  nor nor_4 (nor_4_out, a, not_4_out, not_5_out);
  nor nor_5 (nor_5_out, d, b);
  nor nor_6 (out_5, nor_5_out, nor_1_out, nor_2_out, nor_3_out, nor_4_out);
endmodule
