// Logisim project 3.circ as structural Verilog
module main (
  input  in_1,
  input  in_2,
  output out_3
);

  wire and_1_out, and_2_out, not_1_out, not_2_out;

  not not_1 (not_1_out, in_1);
  and and_1 (and_1_out, not_1_out, in_2);
  and and_2 (and_2_out, in_1, not_2_out);
  not not_2 (not_2_out, in_2);
  or or_1 (out_3, and_1_out, and_2_out);
endmodule

module first (
  input  in_1,
  input  in_2,
  input  in_3,
  input  in_4,
  output out_5
);

  wire main_1_out_3, main_2_out_3;

  main main_1 (.in_1(in_1), .in_2(in_2), .out_3(main_1_out_3));
  main main_2 (.in_1(in_3), .in_2(in_4), .out_3(main_2_out_3));
  main main_3 (.in_1(main_1_out_3), .in_2(main_2_out_3), .out_3(out_5));
endmodule
