// Logisim project 3b.circ as structural Verilog
module main (
  input  x,
  input  y,
  output s,
  output c
);

  xor xor_1 (s, x, y);
  and and_1 (c, x, y);
endmodule

module full_adder (
  input  cin,
  input  x,
  input  y,
  output out_4,
  output out_5
);

  wire main_1_c, main_1_s, main_2_c;

  main main_1 (.x(x), .y(y), .s(main_1_s), .c(main_1_c));
  main main_2 (.x(cin), .y(main_1_s), .s(out_4), .c(main_2_c));
  or or_1 (out_5, main_2_c, main_1_c);
endmodule
