// Logisim project 4a.circ as structural Verilog: 1 circuit, main circuit main
module main (
  input  a,
  input  b,
  output \xor ,
  output out_4
);

  wire nand_1_out, nand_2_out, nand_3_out;

  nand nand_1 (nand_1_out, a, b);
  nand nand_2 (nand_2_out, a, nand_1_out);
  nand nand_3 (nand_3_out, nand_1_out, b);
  nand nand_4 (\xor , nand_2_out, nand_3_out);
  nand nand_5 (out_4, \xor , \xor );
endmodule
