// Logisim project 4b.circ as structural Verilog: 1 circuit, main circuit main
module main (
  input  a,
  input  b,
  output \xnor ,
  output out_4
);

  wire nor_1_out, nor_2_out, nor_3_out;

  nor nor_1 (nor_1_out, a, b);
  nor nor_2 (nor_2_out, a, nor_1_out);
  nor nor_3 (nor_3_out, nor_1_out, b);
  nor nor_4 (\xnor , nor_2_out, nor_3_out);
  nor nor_5 (out_4, \xnor , \xnor );
endmodule
