// Logisim project 1.circ as structural Verilog: 1 circuit, main circuit main
module main (
  input  i0,
  input  i1,
  input  i2,
  input  i3,
  input  En,
  input  s1,
  input  s0,
  output F
);

  wire and_1_out, and_2_out, and_3_out, and_4_out, not_1_out, not_2_out, not_3_out, not_4_out;

  not not_1 (not_1_out, s1);
  not not_2 (not_2_out, s0);
  not not_3 (not_3_out, s0);
  and and_1 (and_1_out, i0, En, not_1_out, not_2_out);
  and and_2 (and_2_out, i1, En, not_4_out, s0);
  not not_4 (not_4_out, s1);
  and and_3 (and_3_out, i2, En, s1, not_3_out);
  and and_4 (and_4_out, i3, En, s1, s0);
  or or_1 (F, and_1_out, and_2_out, and_3_out, and_4_out);
endmodule
