// Logisim project 2.circ as structural Verilog: 1 circuit, main circuit main
module main (
  input  in_1,
  input  [3:0] in_2,
  output [7:0] out_3
);

  Multiplexer #(.select(4), .width(8)) multiplexer_1 (
    .in0({8{1'b0}}), .in1({8{1'b1}}), .in2({8{1'b0}}), .in3({8{1'b0}}), .in4({8{1'b1}}), .in5({8{1'b1}}),
    .in6({8{1'b0}}), .in7({8{1'b0}}), .in8({8{1'b0}}), .in9({8{1'b1}}), .in10({8{1'b1}}), .in11({8{1'b0}}),
    .in12({8{1'b0}}), .in13({8{1'b0}}), .in14({8{1'b1}}), .in15({8{1'b1}}), .out(out_3), .sel(in_2), .en(in_1));
endmodule
