// Logisim project 3.circ as structural Verilog: 1 circuit, main circuit main
module main (
  input  [3:0] x,
  input  in_2,
  input  [1:0] in_3,
  output [3:0] out_4
);

  wire [3:0] not_1_out;

  assign not_1_out = ~x;  // NOT_Gate not_1, 4 bits wide
  Multiplexer #(.select(2), .width(4)) multiplexer_1 (
    .in0(not_1_out), .in1(4'b0000), .in2(x), .in3(4'b1111), .out(out_4), .sel(in_3), .en(in_2));
endmodule
