// Logisim project 4.circ as structural Verilog: 1 circuit, main circuit main
module main (
  input  x,
  input  y,
  input  in_3,
  input  in_4,
  output F
);

  wire and_1_out, not_1_out, or_1_out;

  not not_1 (not_1_out, x);
  and and_1 (and_1_out, x, y);
  or or_1 (or_1_out, not_1_out, and_1_out);
  Multiplexer multiplexer_1 (.in0(or_1_out), .in1(y), .out(F), .sel(in_3), .en(in_4));
endmodule
