// Logisim project 5.circ as structural Verilog: 1 circuit, main circuit main
module main (
  input  [3:0] a,
  input  [3:0] b,
  input  [1:0] in_3,
  input  in_4,
  output [3:0] f
);

  wire [3:0] and_1_out, not_1_out, not_2_out, not_3_out, not_4_out, or_1_out;

  assign not_1_out = ~a;  // NOT_Gate not_1, 4 bits wide
  assign not_2_out = ~b;  // NOT_Gate not_2, 4 bits wide
  assign not_3_out = ~b;  // NOT_Gate not_3, 4 bits wide
  assign not_4_out = ~b;  // NOT_Gate not_4, 4 bits wide
  assign and_1_out = not_1_out & not_2_out;  // AND_Gate and_1, 4 bits wide
  Multiplexer #(.select(2), .width(4)) multiplexer_1 (
    .in0(or_1_out), .in1(not_3_out), .in2(4'b0000), .in3(not_4_out), .out(f), .sel(in_3), .en(in_4));
  assign or_1_out = a | and_1_out;  // OR_Gate or_1, 4 bits wide
endmodule
