// Logisim project 6.circ as structural Verilog: 1 circuit, main circuit main
module main (
  input  in_1,
  input  [1:0] in_2,
  input  in_3,
  input  in_4,
  input  x,
  input  in_6,
  output out_7
);

  wire multiplexer_1_out, multiplexer_2_out;

  Multiplexer #(.select(2)) multiplexer_1 (
    .in1(in_1), .out(multiplexer_1_out), .sel(in_2), .en(in_3));  // open: in0, in2, in3
  Multiplexer #(.select(2)) multiplexer_2 (.out(multiplexer_2_out), .sel(in_2), .en(in_6));  // open: in0, in1, in2, in3
  Multiplexer multiplexer_3 (.in0(multiplexer_1_out), .in1(multiplexer_2_out), .out(out_7), .sel(x), .en(in_4));
endmodule
