// Logisim project 7.circ as structural Verilog: 1 circuit, main circuit main
module main (
  input  [2:0] in_1,
  output [7:0] c,
  output [7:0] s
);

  wire [7:0] demultiplexer_1_out1, demultiplexer_1_out2, demultiplexer_1_out3, demultiplexer_1_out4,
       demultiplexer_1_out5, demultiplexer_1_out6, demultiplexer_1_out7;

  Demultiplexer #(.select(3), .width(8)) demultiplexer_1 (
    .out1(demultiplexer_1_out1), .out2(demultiplexer_1_out2), .out3(demultiplexer_1_out3),
    .out4(demultiplexer_1_out4), .out5(demultiplexer_1_out5), .out6(demultiplexer_1_out6),
    .out7(demultiplexer_1_out7), .in({8{1'b1}}), .sel(in_1), .en(1'b1));  // open: out0
  assign c = demultiplexer_1_out3 | demultiplexer_1_out5 | demultiplexer_1_out6 | demultiplexer_1_out7;  // OR_Gate or_1, 8 bits wide
  assign s = demultiplexer_1_out2 | demultiplexer_1_out1 | demultiplexer_1_out4 | demultiplexer_1_out7;  // OR_Gate or_2, 8 bits wide
endmodule
