// Logisim project solu.circ as structural Verilog: 8 circuits, main circuit main
module main (
  input  i0,
  input  i1,
  input  i2,
  input  i3,
  input  en,
  input  s1,
  input  s0,
  output f
);

  wire and_1_out, and_2_out, and_3_out, and_4_out, not_1_out, not_2_out, not_3_out, not_4_out;

  and and_1 (and_1_out, i0, en, not_1_out, not_2_out);
  not not_1 (not_1_out, s1);
  not not_2 (not_2_out, s0);
  and and_2 (and_2_out, i1, en, not_3_out, s0);
  not not_3 (not_3_out, s1);
  and and_3 (and_3_out, i2, en, s1, not_4_out);
  not not_4 (not_4_out, s0);
  and and_4 (and_4_out, i3, en, s1, s1);
  or or_1 (f, and_1_out, and_2_out, and_3_out, and_4_out);
endmodule

module _2 (
  input  [3:0] in_1,
  output out_2
);

  Multiplexer #(.select(4)) multiplexer_1 (
    .in0(1'b0), .in1(1'b1), .in2(1'b0), .in3(1'b0), .in4(1'b0), .in5(1'b1), .in6(1'b0), .in7(1'b0),
    .in8(1'b0), .in9(1'b1), .in10(1'b1), .in11(1'b0), .in12(1'b0), .in13(1'b0), .in14(1'b1), .in15(1'b1),
    .out(out_2), .sel(in_1));  // open: en
endmodule

module _3 (
  input  in_1,
  input  [1:0] in_2,
  output out_3
);

  wire not_1_out;

  not not_1 (not_1_out, in_1);
  Multiplexer #(.select(2), .enable("false")) multiplexer_1 (
    .in0(not_1_out), .in1(1'b0), .in2(in_1), .in3(1'b1), .out(out_3), .sel(in_2));
endmodule

module _4 (
  input  in_1,
  input  in_2,
  input  in_3,
  output out_4
);

  wire not_1_out, or_1_out;

  not not_1 (not_1_out, in_1);
  or or_1 (or_1_out, in_2, not_1_out);
  Multiplexer #(.enable("false")) multiplexer_1 (.in0(or_1_out), .in1(in_2), .out(out_4), .sel(in_3));
endmodule

module _5 (
  input  in_1,
  input  in_2,
  input  [1:0] in_3,
  output out_4
);

  wire not_1_out, or_1_out;

  not not_1 (not_1_out, in_2);
  or or_1 (or_1_out, in_1, not_1_out);
  Multiplexer #(.select(2)) multiplexer_1 (
    .in0(or_1_out), .in1(not_1_out), .in2(1'b0), .in3(not_1_out), .out(out_4), .sel(in_3));  // open: en
endmodule

module _6 (
  input  in_1,
  input  in_2,
  input  in_3,
  input  in_4,
  input  in_5,
  input  in_6,
  input  in_7,
  input  in_8,
  input  in_9,
  input  [1:0] in_10,
  input  in_11,
  output out_12
);

  wire multiplexer_1_out, multiplexer_2_out;

  Multiplexer #(.select(2), .enable("false")) multiplexer_1 (
    .in0(in_1), .in1(in_2), .in2(in_3), .in3(in_4), .out(multiplexer_1_out), .sel(in_10));
  Multiplexer #(.select(2), .enable("false")) multiplexer_2 (
    .in0(in_5), .in1(in_7), .in2(in_9), .in3(in_11), .out(multiplexer_2_out), .sel(in_10));
  Multiplexer multiplexer_3 (.in0(multiplexer_1_out), .in1(multiplexer_2_out), .out(out_12), .sel(in_8), .en(in_6));
endmodule

module _7 (
  input  [2:0] in_1,
  output out_2,
  output out_3
);

  wire demultiplexer_1_out1, demultiplexer_1_out2, demultiplexer_1_out3, demultiplexer_1_out4,
       demultiplexer_1_out5, demultiplexer_1_out6, demultiplexer_1_out7;

  Demultiplexer #(.select(3)) demultiplexer_1 (
    .out1(demultiplexer_1_out1), .out2(demultiplexer_1_out2), .out3(demultiplexer_1_out3),
    .out4(demultiplexer_1_out4), .out5(demultiplexer_1_out5), .out6(demultiplexer_1_out6),
    .out7(demultiplexer_1_out7), .in(1'b1), .sel(in_1), .en(1'b1));  // open: out0
  or or_1 (out_2, demultiplexer_1_out1, demultiplexer_1_out2, demultiplexer_1_out4, demultiplexer_1_out7);
  or or_2 (out_3, demultiplexer_1_out6, demultiplexer_1_out7, demultiplexer_1_out5, demultiplexer_1_out3);
endmodule

module _8 (
  input  [2:0] in_1,
  output out_2,
  output out_3
);

  wire demultiplexer_1_out0, demultiplexer_1_out3, demultiplexer_1_out4, demultiplexer_1_out5,
       demultiplexer_1_out6;

  Demultiplexer #(.select(3)) demultiplexer_1 (
    .out0(demultiplexer_1_out0), .out3(demultiplexer_1_out3), .out4(demultiplexer_1_out4),
    .out5(demultiplexer_1_out5), .out6(demultiplexer_1_out6), .in(1'b1), .sel(in_1), .en(1'b1));  // open: out1, out2, out7
  nor nor_1 (out_2, demultiplexer_1_out0, demultiplexer_1_out4, demultiplexer_1_out5, demultiplexer_1_out6);
  nor nor_2 (out_3, demultiplexer_1_out0, demultiplexer_1_out3, demultiplexer_1_out5, demultiplexer_1_out6);
endmodule
