// Logisim project 1.circ as structural Verilog: 4 circuits, main circuit main
module main (
  input  in_1,
  input  in_2
);

  wire clock_1_out, nand_1_out, nand_2_out, nand_3_out, nand_4_out;

  Clock clock_1 (.out(clock_1_out));
  nand nand_1 (nand_1_out, in_1, clock_1_out);
  nand nand_2 (nand_2_out, clock_1_out, in_2);
  nand nand_3 (nand_3_out, nand_1_out, nand_4_out);
  nand nand_4 (nand_4_out, nand_2_out, nand_3_out);
endmodule

module jk (
  input  in_1,
  input  in_2
);

  wire clock_1_out, nand_1_out, nand_2_out, nand_3_out, nand_4_out;

  Clock clock_1 (.out(clock_1_out));
  nand nand_1 (nand_1_out, nand_4_out, clock_1_out);
  nand nand_2 (nand_2_out, clock_1_out, nand_3_out);
  nand nand_3 (nand_3_out, nand_1_out, nand_4_out);
  nand nand_4 (nand_4_out, nand_2_out, nand_3_out);
endmodule

module d (
  input  in_1,
  input  in_2,
  input  in_3
);

  wire clock_1_out, j_k_ff_1_q, j_k_ff_1_qn, not_1_out;

  Clock clock_1 (.out(clock_1_out));
  not not_1 (not_1_out, in_1);
  J_K_Flip_Flop j_k_ff_1 (
    .J(in_1), .clk(clock_1_out), .K(not_1_out), .Q(j_k_ff_1_q), .Qn(j_k_ff_1_qn), .preset(in_2), .en(1'b1),
    .reset(in_3));
endmodule

module t (
  input  in_1
);

  wire clock_1_out, j_k_ff_1_q, j_k_ff_1_qn;

  Clock clock_1 (.out(clock_1_out));
  J_K_Flip_Flop j_k_ff_1 (
    .J(in_1), .clk(clock_1_out), .K(in_1), .Q(j_k_ff_1_q), .Qn(j_k_ff_1_qn), .en(1'b1));  // open: preset, reset
endmodule
