// Logisim project 2.circ as structural Verilog: 5 circuits, main circuit main
module main (
);

  wire and_1_out, clock_1_out, j_k_ff_1_q, j_k_ff_1_qn, j_k_ff_2_q, j_k_ff_2_qn, j_k_ff_3_q;

  Clock clock_1 (.out(clock_1_out));
  J_K_Flip_Flop j_k_ff_1 (
    .J(1'b1), .clk(clock_1_out), .K(1'b1), .Q(j_k_ff_1_q), .Qn(j_k_ff_1_qn), .en(1'b1), .reset(and_1_out));  // open: preset
  J_K_Flip_Flop j_k_ff_2 (
    .J(1'b1), .clk(j_k_ff_1_qn), .K(1'b1), .Q(j_k_ff_2_q), .Qn(j_k_ff_2_qn), .en(1'b1), .reset(and_1_out));  // open: preset
  J_K_Flip_Flop j_k_ff_3 (
    .J(1'b1), .clk(j_k_ff_2_qn), .K(1'b1), .Q(j_k_ff_3_q), .en(1'b1), .reset(and_1_out));  // open: Qn, preset
  and and_1 (and_1_out, j_k_ff_3_q, j_k_ff_2_q, j_k_ff_1_q);
endmodule

module _2b (
);

  wire and_1_out, clock_1_out, j_k_ff_1_q, j_k_ff_2_q, j_k_ff_3_q;

  Clock clock_1 (.out(clock_1_out));
  J_K_Flip_Flop #(.trigger("falling")) j_k_ff_1 (
    .J(1'b1), .clk(clock_1_out), .K(1'b1), .Q(j_k_ff_1_q), .en(1'b1), .reset(and_1_out));  // open: Qn, preset
  J_K_Flip_Flop #(.trigger("falling")) j_k_ff_2 (
    .J(1'b1), .clk(j_k_ff_1_q), .K(1'b1), .Q(j_k_ff_2_q), .en(1'b1), .reset(and_1_out));  // open: Qn, preset
  J_K_Flip_Flop #(.trigger("falling")) j_k_ff_3 (
    .J(1'b1), .clk(j_k_ff_2_q), .K(1'b1), .Q(j_k_ff_3_q), .en(1'b1));  // open: Qn, preset, reset
  and and_1 (and_1_out, j_k_ff_2_q, j_k_ff_1_q);
endmodule

module _2c (
);

  wire and_1_out, clock_1_out, j_k_ff_1_q, j_k_ff_2_q, j_k_ff_2_qn, j_k_ff_3_qn;

  Clock clock_1 (.out(clock_1_out));
  J_K_Flip_Flop #(.trigger("falling")) j_k_ff_1 (
    .J(j_k_ff_3_qn), .clk(clock_1_out), .K(j_k_ff_3_qn), .Q(j_k_ff_1_q), .en(1'b1));  // open: Qn, preset, reset
  J_K_Flip_Flop #(.trigger("falling")) j_k_ff_2 (
    .J(1'b1), .clk(j_k_ff_1_q), .K(1'b1), .Q(j_k_ff_2_q), .Qn(j_k_ff_2_qn), .en(1'b1));  // open: preset, reset
  and and_1 (and_1_out, j_k_ff_1_q, j_k_ff_2_q);
  J_K_Flip_Flop #(.trigger("falling")) j_k_ff_3 (
    .J(and_1_out), .clk(clock_1_out), .K(j_k_ff_2_qn), .Qn(j_k_ff_3_qn), .en(1'b1));  // open: Q, preset, reset
endmodule

module _2d (
);

  wire clock_1_out, j_k_ff_1_q, j_k_ff_1_qn, j_k_ff_2_q, j_k_ff_2_qn, j_k_ff_3_q, j_k_ff_3_qn, j_k_ff_4_q,
       j_k_ff_4_qn;

  Clock clock_1 (.out(clock_1_out));
  J_K_Flip_Flop #(.trigger("falling")) j_k_ff_1 (
    .J(j_k_ff_4_qn), .clk(clock_1_out), .K(j_k_ff_4_q), .Q(j_k_ff_1_q), .Qn(j_k_ff_1_qn), .en(1'b1));  // open: preset, reset
  J_K_Flip_Flop #(.trigger("falling")) j_k_ff_2 (
    .J(j_k_ff_1_q), .clk(clock_1_out), .K(j_k_ff_1_qn), .Q(j_k_ff_2_q), .Qn(j_k_ff_2_qn), .en(1'b1));  // open: preset, reset
  J_K_Flip_Flop #(.trigger("falling")) j_k_ff_3 (
    .J(j_k_ff_2_q), .clk(clock_1_out), .K(j_k_ff_2_qn), .Q(j_k_ff_3_q), .Qn(j_k_ff_3_qn), .en(1'b1));  // open: preset, reset
  J_K_Flip_Flop #(.trigger("falling")) j_k_ff_4 (
    .J(j_k_ff_3_q), .clk(clock_1_out), .K(j_k_ff_3_qn), .Q(j_k_ff_4_q), .Qn(j_k_ff_4_qn), .en(1'b1));  // open: preset, reset
endmodule

module _2e (
);

  wire and_1_out, and_2_out, and_3_out, and_4_out, clock_1_out, j_k_ff_1_q, j_k_ff_1_qn, j_k_ff_2_q,
       j_k_ff_3_q, j_k_ff_3_qn, or_1_out, or_2_out;

  and and_1 (and_1_out, j_k_ff_2_q, j_k_ff_3_qn);
  Clock clock_1 (.out(clock_1_out));
  J_K_Flip_Flop #(.trigger("falling")) j_k_ff_1 (
    .J(and_1_out), .clk(clock_1_out), .K(1'b1), .Q(j_k_ff_1_q), .Qn(j_k_ff_1_qn), .en(1'b1));  // open: preset, reset
  and and_2 (and_2_out, j_k_ff_1_q, j_k_ff_3_q);
  and and_3 (and_3_out, j_k_ff_1_qn, j_k_ff_3_qn);
  or or_1 (or_1_out, and_3_out, and_2_out);
  J_K_Flip_Flop #(.trigger("falling")) j_k_ff_2 (
    .J(or_1_out), .clk(clock_1_out), .K(1'b1), .Q(j_k_ff_2_q), .en(1'b1));  // open: Qn, preset, reset
  or or_2 (or_2_out, j_k_ff_2_q, j_k_ff_1_qn);
  and and_4 (and_4_out, j_k_ff_2_q, j_k_ff_1_qn);
  J_K_Flip_Flop #(.trigger("falling")) j_k_ff_3 (
    .J(and_4_out), .clk(clock_1_out), .K(or_2_out), .Q(j_k_ff_3_q), .Qn(j_k_ff_3_qn), .en(1'b1));  // open: preset, reset
endmodule
