// Logisim project 1.circ as structural Verilog: 1 circuit, main circuit main
module main (
  input  X,
  input  Y,
  output A,
  output B,
  output c,
  output D
);

  wire not_1_out;

  not not_1 (not_1_out, Y);
  and and_1 (A, Y, X);
  and and_2 (B, X, not_1_out);

  assign c = 1'b0;
  assign D = Y;
endmodule
