// Logisim project 11.circ as structural Verilog
module main (
  input  x,
  input  y,
  output s,
  output c
);

  xor xor_1 (s, x, y);
  and and_1 (c, x, y);
endmodule

module full_adder (
  input  cin,
  input  x,
  input  y,
  output s,
  output cout
);

  wire main_1_c, main_1_s, main_2_c;

  main main_1 (.x(x), .y(y), .s(main_1_s), .c(main_1_c));
  main main_2 (.x(cin), .y(main_1_s), .s(s), .c(main_2_c));
  or or_1 (cout, main_2_c, main_1_c);
endmodule

module _4_bit_adder (
  input  a0,
  input  a1,
  input  a2,
  input  a3,
  input  b0,
  input  b1,
  input  b2,
  input  b3,
  input  in_9,
  output s0,
  output s1,
  output s2,
  output s3,
  output c4
);

  wire full_adder_1_cout, full_adder_2_cout, full_adder_3_cout;

  full_adder full_adder_1 (.cin(in_9), .x(a0), .y(b0), .s(s0), .cout(full_adder_1_cout));
  full_adder full_adder_2 (.cin(full_adder_1_cout), .x(a1), .y(b1), .s(s1), .cout(full_adder_2_cout));
  full_adder full_adder_3 (.cin(full_adder_2_cout), .x(a2), .y(b2), .s(s2), .cout(full_adder_3_cout));
  full_adder full_adder_4 (.cin(full_adder_3_cout), .x(a3), .y(b3), .s(s3), .cout(c4));
endmodule

module _4_bit_adder_substractor (
  input  control_in,
  input  in_2,
  input  in_3,
  input  in_4,
  input  in_5,
  input  a0,
  input  a1,
  input  a2,
  input  a3,
  output out_10,
  output out_11,
  output out_12,
  output out_13
);

  wire xor_1_out, xor_2_out, xor_3_out, xor_4_out;

  xor xor_1 (xor_1_out, control_in, in_3);
  xor xor_2 (xor_2_out, control_in, in_2);
  xor xor_3 (xor_3_out, control_in, in_4);
  xor xor_4 (xor_4_out, control_in, in_5);
  _4_bit_adder u_4_bit_adder_1 (
    .in_9(control_in), .a0(a0), .a1(a1), .a2(a2), .a3(a2), .b0(xor_2_out), .b1(xor_1_out), .b2(xor_3_out),
    .b3(xor_4_out), .s0(out_10), .s1(out_11), .s2(out_12), .s3(out_13));  // open: c4

  assign a3 = a2;
endmodule

module _1_digit_bcd_adder (
  input  A0,
  input  A1,
  input  A2,
  input  A3,
  input  B0,
  input  B1,
  input  B2,
  input  B3,
  input  in_9,
  output C,
  output S0,
  output S1,
  output S2,
  output S3
);

  wire and_1_out, and_2_out, n4_bit_adder_1_c4, n4_bit_adder_1_s0, n4_bit_adder_1_s1, n4_bit_adder_1_s2,
       n4_bit_adder_1_s3, n4_bit_adder_2_c4;

  _4_bit_adder u_4_bit_adder_1 (
    .in_9(in_9), .a0(A0), .a1(A1), .a2(A2), .a3(A3), .b0(B0), .b1(B1), .b2(B2), .b3(B3),
    .s0(n4_bit_adder_1_s0), .s1(n4_bit_adder_1_s1), .s2(n4_bit_adder_1_s2), .s3(n4_bit_adder_1_s3),
    .c4(n4_bit_adder_1_c4));
  and and_1 (and_1_out, n4_bit_adder_1_s1, n4_bit_adder_1_s3);
  and and_2 (and_2_out, n4_bit_adder_1_s2, n4_bit_adder_1_s3);
  _4_bit_adder u_4_bit_adder_2 (
    .in_9(1'b0), .a0(n4_bit_adder_1_s0), .a1(n4_bit_adder_1_s1), .a2(n4_bit_adder_1_s2),
    .a3(n4_bit_adder_1_s3), .b0(1'b0), .b1(C), .b2(C), .b3(1'b0), .s0(S0), .s1(S1), .s2(S2), .s3(S3),
    .c4(n4_bit_adder_2_c4));
  or or_1 (C, n4_bit_adder_1_c4, and_1_out, and_2_out);
endmodule

module _4_digit_bcd_adder (
  input  in_1,
  input  in_2,
  input  in_3,
  input  in_4,
  input  in_5,
  input  in_6,
  input  in_7,
  input  in_8,
  input  in_9,
  input  in_10,
  input  in_11,
  input  in_12,
  input  in_13,
  input  in_14,
  input  in_15,
  input  in_16,
  input  in_17,
  input  in_18,
  input  in_19,
  input  in_20,
  input  in_21,
  input  in_22,
  input  in_23,
  input  in_24,
  input  in_25,
  input  in_26,
  input  in_27,
  input  in_28,
  input  in_29,
  input  in_30,
  input  in_31,
  input  in_32,
  input  in_33
);

  wire n1_digit_bcd_adder_1_c, n1_digit_bcd_adder_1_s0, n1_digit_bcd_adder_1_s1, n1_digit_bcd_adder_1_s2,
       n1_digit_bcd_adder_1_s3, n1_digit_bcd_adder_2_c, n1_digit_bcd_adder_2_s0, n1_digit_bcd_adder_2_s1,
       n1_digit_bcd_adder_2_s2, n1_digit_bcd_adder_2_s3, n1_digit_bcd_adder_3_c, n1_digit_bcd_adder_3_s0,
       n1_digit_bcd_adder_3_s1, n1_digit_bcd_adder_3_s2, n1_digit_bcd_adder_3_s3, n1_digit_bcd_adder_4_c,
       n1_digit_bcd_adder_4_s0, n1_digit_bcd_adder_4_s1, n1_digit_bcd_adder_4_s2, n1_digit_bcd_adder_4_s3;

  _1_digit_bcd_adder u_1_digit_bcd_adder_1 (
    .in_9(in_17), .A0(in_1), .A1(in_2), .A2(in_3), .A3(in_4), .B0(in_18), .B1(in_19), .B2(in_20), .B3(in_21),
    .C(n1_digit_bcd_adder_1_c), .S0(n1_digit_bcd_adder_1_s0), .S1(n1_digit_bcd_adder_1_s1),
    .S2(n1_digit_bcd_adder_1_s2), .S3(n1_digit_bcd_adder_1_s3));
  _1_digit_bcd_adder u_1_digit_bcd_adder_2 (
    .in_9(n1_digit_bcd_adder_1_c), .A0(in_5), .A1(in_6), .A2(in_7), .A3(in_8), .B0(in_22), .B1(in_23),
    .B2(in_24), .B3(in_25), .C(n1_digit_bcd_adder_2_c), .S0(n1_digit_bcd_adder_2_s0),
    .S1(n1_digit_bcd_adder_2_s1), .S2(n1_digit_bcd_adder_2_s2), .S3(n1_digit_bcd_adder_2_s3));
  _1_digit_bcd_adder u_1_digit_bcd_adder_3 (
    .in_9(n1_digit_bcd_adder_2_c), .A0(in_9), .A1(in_10), .A2(in_11), .A3(in_12), .B0(in_26), .B1(in_27),
    .B2(in_28), .B3(in_29), .C(n1_digit_bcd_adder_3_c), .S0(n1_digit_bcd_adder_3_s0),
    .S1(n1_digit_bcd_adder_3_s1), .S2(n1_digit_bcd_adder_3_s2), .S3(n1_digit_bcd_adder_3_s3));
  _1_digit_bcd_adder u_1_digit_bcd_adder_4 (
    .in_9(n1_digit_bcd_adder_3_c), .A0(in_13), .A1(in_14), .A2(in_15), .A3(in_16), .B0(in_30), .B1(in_31),
    .B2(in_32), .B3(in_33), .C(n1_digit_bcd_adder_4_c), .S0(n1_digit_bcd_adder_4_s0),
    .S1(n1_digit_bcd_adder_4_s1), .S2(n1_digit_bcd_adder_4_s2), .S3(n1_digit_bcd_adder_4_s3));
endmodule

module _4_bit_bcd_to_excess_3 (
  input  a0,
  input  a1,
  input  a2,
  input  a3,
  input  in_5,
  output s3,
  output s2,
  output s1,
  output s0,
  output out_10
);

  _4_bit_adder u_4_bit_adder_1 (
    .in_9(in_5), .a0(a0), .a1(a1), .a2(a2), .a3(a3), .b0(1'b1), .b1(1'b1), .b2(1'b0), .b3(1'b0), .s0(s0),
    .s1(s1), .s2(s2), .s3(s3), .c4(out_10));
endmodule

module _1_digit_excess_3_adder (
  input  in_1,
  input  in_2,
  input  in_3,
  input  in_4,
  input  in_5,
  input  in_6,
  input  in_7,
  input  in_8,
  input  in_9,
  input  in_10,
  input  in_11,
  input  in_12,
  output out_13,
  output out_14,
  output out_15,
  output out_16,
  output out_17,
  output out_18,
  output out_19
);

  wire and_1_out, and_2_out, and_3_out, and_4_out, and_5_out, and_6_out, and_7_out, and_8_out,
       n4_bit_adder_1_c4, n4_bit_adder_1_s0, n4_bit_adder_1_s1, n4_bit_adder_1_s2, n4_bit_adder_1_s3,
       n4_bit_bcd_to_excess_3_1_s0, n4_bit_bcd_to_excess_3_1_s1, n4_bit_bcd_to_excess_3_1_s2,
       n4_bit_bcd_to_excess_3_1_s3, n4_bit_bcd_to_excess_3_2_s0, n4_bit_bcd_to_excess_3_2_s1,
       n4_bit_bcd_to_excess_3_2_s2, n4_bit_bcd_to_excess_3_2_s3, not_1_out, or_1_out, or_2_out, or_3_out,
       or_4_out;

  _4_bit_bcd_to_excess_3 u_4_bit_bcd_to_excess_3_1 (
    .in_5(in_9), .a0(in_1), .a1(in_2), .a2(in_3), .a3(in_4), .s3(n4_bit_bcd_to_excess_3_1_s3),
    .s2(n4_bit_bcd_to_excess_3_1_s2), .s1(n4_bit_bcd_to_excess_3_1_s1), .s0(n4_bit_bcd_to_excess_3_1_s0),
    .out_10(out_13));
  _4_bit_adder u_4_bit_adder_1 (
    .in_9(in_11), .a0(n4_bit_bcd_to_excess_3_1_s0), .a1(n4_bit_bcd_to_excess_3_1_s1),
    .a2(n4_bit_bcd_to_excess_3_1_s2), .a3(n4_bit_bcd_to_excess_3_1_s3), .b0(n4_bit_bcd_to_excess_3_2_s0),
    .b1(n4_bit_bcd_to_excess_3_2_s1), .b2(n4_bit_bcd_to_excess_3_2_s2), .b3(n4_bit_bcd_to_excess_3_2_s3),
    .s0(n4_bit_adder_1_s0), .s1(n4_bit_adder_1_s1), .s2(n4_bit_adder_1_s2), .s3(n4_bit_adder_1_s3),
    .c4(n4_bit_adder_1_c4));
  _4_bit_bcd_to_excess_3 u_4_bit_bcd_to_excess_3_2 (
    .in_5(in_10), .a0(in_5), .a1(in_6), .a2(in_7), .a3(in_8), .s3(n4_bit_bcd_to_excess_3_2_s3),
    .s2(n4_bit_bcd_to_excess_3_2_s2), .s1(n4_bit_bcd_to_excess_3_2_s1), .s0(n4_bit_bcd_to_excess_3_2_s0),
    .out_10(out_14));
  and and_1 (and_1_out, n4_bit_adder_1_c4, 1'b1);
  _4_bit_adder u_4_bit_adder_2 (
    .in_9(in_12), .a0(n4_bit_adder_1_s0), .a1(n4_bit_adder_1_s1), .a2(n4_bit_adder_1_s2),
    .a3(n4_bit_adder_1_s3), .b0(or_1_out), .b1(or_2_out), .b2(or_3_out), .b3(or_4_out), .s0(out_19),
    .s1(out_18), .s2(out_17), .s3(out_16), .c4(out_15));
  and and_2 (and_2_out, n4_bit_adder_1_c4, 1'b1);
  and and_3 (and_3_out, n4_bit_adder_1_c4, 1'b0);
  or or_1 (or_1_out, and_1_out, and_5_out);
  not not_1 (not_1_out, n4_bit_adder_1_c4);
  and and_4 (and_4_out, 1'b0, n4_bit_adder_1_c4);
  or or_2 (or_2_out, and_2_out, and_6_out);
  and and_5 (and_5_out, not_1_out, 1'b1);
  or or_3 (or_3_out, and_3_out, and_7_out);
  or or_4 (or_4_out, and_4_out, and_8_out);
  and and_6 (and_6_out, not_1_out, 1'b0);
  and and_7 (and_7_out, not_1_out, 1'b1);
  and and_8 (and_8_out, not_1_out, 1'b1);
endmodule
