// Logisim project 3.circ as structural Verilog: 1 circuit, main circuit main
module main (
  input  in_1,
  input  in_2,
  input  in_3,
  input  in_4,
  input  in_5,
  input  in_6,
  output out_7
);

  wire and_1_out, and_2_out, and_3_out, and_4_out, and_5_out, not_1_out, not_2_out, not_3_out, not_4_out,
       not_5_out, not_6_out, not_7_out, not_8_out, not_9_out, not_10_out, not_11_out, not_12_out, not_13_out,
       not_14_out, not_15_out, not_16_out, not_17_out, not_18_out;

  not not_1 (not_1_out, in_1);
  not not_2 (not_2_out, in_2);
  not not_3 (not_3_out, in_3);
  not not_4 (not_4_out, in_4);
  not not_5 (not_5_out, in_5);
  not not_6 (not_6_out, in_1);
  not not_7 (not_7_out, in_2);
  not not_8 (not_8_out, in_3);
  not not_9 (not_9_out, in_5);
  not not_10 (not_10_out, in_1);
  not not_11 (not_11_out, in_2);
  not not_12 (not_12_out, in_4);
  not not_13 (not_13_out, in_5);
  not not_14 (not_14_out, in_1);
  not not_15 (not_15_out, in_2);
  not not_16 (not_16_out, in_1);
  not not_17 (not_17_out, in_3);
  not not_18 (not_18_out, in_5);
  and and_1 (and_1_out, not_1_out, not_2_out, not_3_out, not_4_out, not_5_out, in_6);
  and and_2 (and_2_out, not_6_out, not_7_out, not_8_out, in_4, not_9_out, in_6);
  and and_3 (and_3_out, not_10_out, not_11_out, in_3, not_12_out, not_13_out, in_6);
  and and_4 (and_4_out, not_14_out, not_15_out, in_3, in_4, in_5, in_6);
  and and_5 (and_5_out, not_16_out, in_2, not_17_out, in_4, not_18_out, in_6);
  or or_1 (out_7, and_1_out, and_2_out, and_3_out, and_4_out, and_5_out);
endmodule
