// Logisim project 5.circ as structural Verilog
module main (
  input  x,
  input  y,
  output s,
  output c
);

  xor xor_1 (s, x, y);
  and and_1 (c, x, y);
endmodule

module full_adder (
  input  cin,
  input  x,
  input  y,
  output s,
  output cout
);

  wire main_1_c, main_1_s, main_2_c;

  main main_1 (.x(x), .y(y), .s(main_1_s), .c(main_1_c));
  main main_2 (.x(cin), .y(main_1_s), .s(s), .c(main_2_c));
  or or_1 (cout, main_2_c, main_1_c);
endmodule

module _4_bit_adder (
  input  a0,
  input  a1,
  input  a2,
  input  a3,
  input  b0,
  input  b1,
  input  b2,
  input  b3,
  output out_9,
  output out_10,
  output out_11,
  output out_12,
  output c4
);

  wire full_adder_1_cout, full_adder_2_cout, full_adder_3_cout;

  full_adder full_adder_1 (.cin(1'b0), .x(a0), .y(b0), .s(out_9), .cout(full_adder_1_cout));
  full_adder full_adder_2 (.cin(full_adder_1_cout), .x(a1), .y(b1), .s(out_10), .cout(full_adder_2_cout));
  full_adder full_adder_3 (.cin(full_adder_2_cout), .x(a2), .y(b2), .s(out_11), .cout(full_adder_3_cout));
  full_adder full_adder_4 (.cin(full_adder_3_cout), .x(a3), .y(b3), .s(out_12), .cout(c4));
endmodule
