// Logisim project 6a.circ as structural Verilog
module main (
  input  x,
  input  y,
  output s,
  output c
);

  xor xor_1 (s, x, y);
  and and_1 (c, x, y);
endmodule

module full_adder (
  input  cin,
  input  x,
  input  y,
  output s,
  output cout
);

  wire main_1_c, main_1_s, main_2_c;

  main main_1 (.x(x), .y(y), .s(main_1_s), .c(main_1_c));
  main main_2 (.x(cin), .y(main_1_s), .s(s), .c(main_2_c));
  or or_1 (cout, main_2_c, main_1_c);
endmodule

module _4_bit_adder (
  input  a0,
  input  a1,
  input  a2,
  input  a3,
  input  b0,
  input  b1,
  input  b2,
  input  b3,
  input  in_9,
  output s0,
  output s1,
  output s2,
  output s3,
  output c4
);

  wire full_adder_1_cout, full_adder_2_cout, full_adder_3_cout;

  full_adder full_adder_1 (.cin(in_9), .x(a0), .y(b0), .s(s0), .cout(full_adder_1_cout));
  full_adder full_adder_2 (.cin(full_adder_1_cout), .x(a1), .y(b1), .s(s1), .cout(full_adder_2_cout));
  full_adder full_adder_3 (.cin(full_adder_2_cout), .x(a2), .y(b2), .s(s2), .cout(full_adder_3_cout));
  full_adder full_adder_4 (.cin(full_adder_3_cout), .x(a3), .y(b3), .s(s3), .cout(c4));
endmodule

module _4_bit_adder_substractor (
  input  control_in,
  input  in_2,
  input  in_3,
  input  in_4,
  input  in_5,
  input  a0,
  input  a1,
  input  a2,
  input  a3,
  output out_10,
  output out_11,
  output out_12,
  output out_13
);

  wire n4_bit_adder_1_c4, n4_bit_adder_1_s0, n4_bit_adder_1_s1, n4_bit_adder_1_s2, n4_bit_adder_1_s3,
       not_1_out, xor_1_out, xor_2_out, xor_3_out, xor_4_out;

  xor xor_1 (xor_1_out, control_in, in_3);
  xor xor_2 (xor_2_out, control_in, in_2);
  xor xor_3 (xor_3_out, control_in, in_4);
  xor xor_4 (xor_4_out, control_in, in_5);
  _4_bit_adder u_4_bit_adder_1 (
    .in_9(control_in), .a0(a0), .a1(a1), .a2(a2), .a3(a2), .b0(xor_2_out), .b1(xor_1_out), .b2(xor_3_out),
    .b3(xor_4_out), .s0(n4_bit_adder_1_s0), .s1(n4_bit_adder_1_s1), .s2(n4_bit_adder_1_s2),
    .s3(n4_bit_adder_1_s3), .c4(n4_bit_adder_1_c4));
  not not_1 (not_1_out, n4_bit_adder_1_c4);
  xor xor_5 (out_10, not_1_out, n4_bit_adder_1_s0);
  xor xor_6 (out_11, n4_bit_adder_1_s1, not_1_out);
  xor xor_7 (out_12, not_1_out, n4_bit_adder_1_s2);
  xor xor_8 (out_13, not_1_out, n4_bit_adder_1_s3);

  assign a3 = a2;
endmodule
