// Logisim project GAURANG_KAVI_LAB5.circ as structural Verilog: 13 circuits, main circuit Lab5.1.
module Lab5_1 (
  input  I0,
  input  I1,
  output O0,
  output O1,
  output O3,
  output O4
);

  wire not_1_out;

  not not_1 (not_1_out, I1);
  and and_1 (O0, I0, I1);
  and and_2 (O1, I0, not_1_out);
  not not_2 (O3, 1'b1);

  assign O4 = I1;
endmodule

module XOR (
  input  A,
  input  B,
  output out_3
);

  wire and_1_out, and_2_out, not_1_out, not_2_out;

  not not_1 (not_1_out, A);
  not not_2 (not_2_out, B);
  and and_1 (and_1_out, not_1_out, B);
  and and_2 (and_2_out, not_2_out, A);
  or or_1 (out_3, and_1_out, and_2_out);
endmodule

module Lab5_2 (
  input  A,
  input  B,
  input  C,
  input  D,
  output out_5,
  output out_6,
  output out_7
);

  wire and_1_out, and_2_out, and_3_out, and_4_out, and_5_out, not_1_out, not_2_out, not_3_out, not_4_out,
       or_1_out, xor_1_out_3, xor_2_out_3;

  not not_1 (not_1_out, B);
  not not_2 (not_2_out, C);
  not not_3 (not_3_out, D);
  not not_4 (not_4_out, A);
  XOR xor_1 (.A(A), .B(B), .out_3(xor_1_out_3));
  or or_1 (or_1_out, C, D);
  and and_1 (and_1_out, A, not_1_out);
  and and_2 (and_2_out, A, not_2_out, not_3_out);
  and and_3 (and_3_out, not_1_out, C, D);
  XOR xor_2 (.A(C), .B(D), .out_3(xor_2_out_3));
  and and_4 (and_4_out, not_1_out, xor_2_out_3);
  and and_5 (and_5_out, not_4_out, B, D, C);
  and and_6 (out_5, A, B, or_1_out);
  or or_2 (out_6, xor_1_out_3, and_2_out, and_3_out);
  or or_3 (out_7, and_1_out, and_2_out, and_4_out, and_5_out);
endmodule

module Lab5_3 (
  input  S5,
  input  S4,
  input  S3,
  input  S2,
  input  S1,
  input  S0,
  output out_7
);

  wire and_1_out, and_2_out, and_3_out, not_1_out, not_2_out, not_3_out, not_4_out, not_5_out;

  not not_1 (not_1_out, S5);
  not not_2 (not_2_out, S4);
  not not_3 (not_3_out, S3);
  not not_4 (not_4_out, S2);
  not not_5 (not_5_out, S1);
  and and_1 (and_1_out, not_1_out, S0, not_2_out, not_4_out, not_5_out);
  and and_2 (and_2_out, not_1_out, S0, S2, not_5_out, not_3_out);
  and and_3 (and_3_out, S3, S1, S2, not_2_out, S0, not_1_out);
  or or_1 (out_7, and_1_out, and_2_out, and_3_out);
endmodule

module Lab5_4 (
  input  X3,
  input  X2,
  input  X1,
  input  X0,
  output out_5
);

  wire and_1_out, and_2_out, and_3_out, not_1_out, not_2_out, not_3_out, not_4_out, xor_1_out_3;

  not not_1 (not_1_out, X3);
  XOR xor_1 (.A(X3), .B(X2), .out_3(xor_1_out_3));
  not not_2 (not_2_out, X2);
  not not_3 (not_3_out, X1);
  not not_4 (not_4_out, X0);
  and and_1 (and_1_out, not_1_out, not_2_out, not_4_out);
  and and_2 (and_2_out, xor_1_out_3, not_3_out, not_4_out);
  and and_3 (and_3_out, not_1_out, not_2_out, not_3_out, X0);
  or or_1 (out_5, and_1_out, and_3_out, and_2_out);
endmodule

module Full_Adder (
  input  B,
  input  A,
  input  Cin,
  output Sout,
  output Cout
);

  wire and_1_out, and_2_out, xor_1_out_3;

  XOR xor_1 (.A(B), .B(A), .out_3(xor_1_out_3));
  and and_1 (and_1_out, B, A);
  XOR xor_2 (.A(xor_1_out_3), .B(Cin), .out_3(Sout));
  and and_2 (and_2_out, xor_1_out_3, Cin);
  or or_1 (Cout, and_1_out, and_2_out);
endmodule

module Lab5_5 (
  input  a0,
  input  b0,
  input  a1,
  input  b1,
  input  a2,
  input  b2,
  input  a3,
  input  b3,
  output s0,
  output s1,
  output s2,
  output s3,
  output cout
);

  wire full_adder_1_cout, full_adder_2_cout, full_adder_3_cout, not_1_out;

  not not_1 (not_1_out, 1'b1);
  Full_Adder full_adder_1 (.B(not_1_out), .A(a0), .Cin(b0), .Sout(s0), .Cout(full_adder_1_cout));
  Full_Adder full_adder_2 (.B(full_adder_1_cout), .A(a1), .Cin(b1), .Sout(s1), .Cout(full_adder_2_cout));
  Full_Adder full_adder_3 (.B(full_adder_2_cout), .A(a2), .Cin(b2), .Sout(s2), .Cout(full_adder_3_cout));
  Full_Adder full_adder_4 (.B(full_adder_3_cout), .A(a3), .Cin(b3), .Sout(s3), .Cout(cout));
endmodule

module Lab5_6 (
  input  in_1,
  input  in_2,
  input  in_3,
  input  in_4,
  input  in_5,
  input  in_6,
  input  in_7,
  input  in_8,
  input  in_9,
  output out_10,
  output out_11,
  output out_12,
  output out_13,
  output out_14
);

  wire full_adder_1_cout, full_adder_2_cout, full_adder_3_cout, xor_1_out_3, xor_2_out_3, xor_3_out_3,
       xor_4_out_3;

  XOR xor_1 (.A(in_3), .B(in_1), .out_3(xor_1_out_3));
  XOR xor_2 (.A(in_5), .B(in_1), .out_3(xor_2_out_3));
  XOR xor_3 (.A(in_7), .B(in_1), .out_3(xor_3_out_3));
  XOR xor_4 (.A(in_9), .B(in_1), .out_3(xor_4_out_3));
  Full_Adder full_adder_1 (.B(in_1), .A(in_2), .Cin(xor_1_out_3), .Sout(out_10), .Cout(full_adder_1_cout));
  Full_Adder full_adder_2 (.B(full_adder_1_cout), .A(in_4), .Cin(xor_2_out_3), .Sout(out_11), .Cout(full_adder_2_cout));
  Full_Adder full_adder_3 (.B(full_adder_2_cout), .A(in_6), .Cin(xor_3_out_3), .Sout(out_12), .Cout(full_adder_3_cout));
  Full_Adder full_adder_4 (.B(full_adder_3_cout), .A(in_8), .Cin(xor_4_out_3), .Sout(out_13), .Cout(out_14));
endmodule

module Lab5_7 (
  input  in_1,
  input  in_2,
  input  in_3,
  input  in_4,
  input  in_5,
  input  in_6,
  input  in_7,
  input  in_8,
  input  in_9,
  input  in_10,
  input  in_11,
  input  in_12,
  input  in_13,
  input  in_14,
  input  in_15,
  input  in_16,
  input  in_17,
  input  in_18,
  input  in_19,
  input  in_20,
  input  in_21,
  input  in_22,
  input  in_23,
  input  in_24,
  input  in_25,
  output out_26,
  output out_27,
  output out_28,
  output out_29,
  output out_30,
  output out_31,
  output out_32,
  output out_33,
  output out_34,
  output out_35,
  output out_36,
  output out_37,
  output out_38
);

  wire lab5_6_1_out_14, lab5_6_2_out_14;

  Lab5_6 lab5_6_1 (
    .in_1(in_1), .in_2(in_2), .in_3(in_3), .in_4(in_4), .in_5(in_5), .in_6(in_6), .in_7(in_7), .in_8(in_8),
    .in_9(in_9), .out_10(out_26), .out_11(out_27), .out_12(out_28), .out_13(out_29), .out_14(lab5_6_1_out_14));
  Lab5_6 lab5_6_2 (
    .in_1(lab5_6_1_out_14), .in_2(in_10), .in_3(in_11), .in_4(in_12), .in_5(in_13), .in_6(in_14),
    .in_7(in_15), .in_8(in_16), .in_9(in_17), .out_10(out_30), .out_11(out_31), .out_12(out_32),
    .out_13(out_33), .out_14(lab5_6_2_out_14));
  Lab5_6 lab5_6_3 (
    .in_1(lab5_6_2_out_14), .in_2(in_18), .in_3(in_19), .in_4(in_20), .in_5(in_21), .in_6(in_22),
    .in_7(in_23), .in_8(in_24), .in_9(in_25), .out_10(out_34), .out_11(out_35), .out_12(out_36),
    .out_13(out_37), .out_14(out_38));
endmodule

module Lab5_8 (
  input  in_1,
  input  in_2,
  input  in_3,
  input  in_4,
  input  in_5,
  input  in_6,
  input  in_7,
  input  in_8,
  input  SSS,
  output out_10,
  output out_11,
  output out_12,
  output out_13,
  output Cout
);

  wire and_1_out, and_2_out, lab5_5_1_cout, lab5_5_1_s0, lab5_5_1_s1, lab5_5_1_s2, lab5_5_1_s3, not_1_out,
       or_1_out;

  not not_1 (not_1_out, 1'b1);
  Lab5_5 lab5_5_1 (
    .a0(in_1), .b0(in_2), .a1(in_3), .b1(in_4), .a2(in_5), .b2(in_6), .a3(in_7), .b3(in_8), .s0(lab5_5_1_s0),
    .s1(lab5_5_1_s1), .s2(lab5_5_1_s2), .s3(lab5_5_1_s3), .cout(lab5_5_1_cout));
  Lab5_5 lab5_5_2 (
    .a0(lab5_5_1_s0), .b0(SSS), .a1(lab5_5_1_s1), .b1(or_1_out), .a2(lab5_5_1_s2), .b2(or_1_out),
    .a3(lab5_5_1_s3), .b3(not_1_out), .s0(out_10), .s1(out_11), .s2(out_12), .s3(out_13), .cout(Cout));
  and and_1 (and_1_out, lab5_5_1_s2, lab5_5_1_s3);
  and and_2 (and_2_out, lab5_5_1_s1, lab5_5_1_s3);
  or or_1 (or_1_out, and_1_out, lab5_5_1_cout, and_2_out);
endmodule

module Lab5_9 (
  input  in_1,
  input  in_2,
  input  in_3,
  input  in_4,
  input  in_5,
  input  in_6,
  input  in_7,
  input  in_8,
  input  in_9,
  input  in_10,
  input  in_11,
  input  in_12,
  input  in_13,
  input  in_14,
  input  in_15,
  input  in_16,
  input  in_17,
  input  in_18,
  input  in_19,
  input  in_20,
  input  in_21,
  input  in_22,
  input  in_23,
  input  in_24,
  input  in_25,
  input  in_26,
  input  in_27,
  input  in_28,
  input  in_29,
  input  in_30,
  input  in_31,
  input  in_32,
  input  in_33,
  output out_34,
  output out_35,
  output out_36,
  output out_37,
  output out_38,
  output out_39,
  output out_40,
  output out_41,
  output out_42,
  output out_43,
  output out_44,
  output out_45,
  output out_46,
  output out_47,
  output out_48,
  output out_49,
  output out_50
);

  wire lab5_8_1_cout, lab5_8_2_cout, lab5_8_3_cout;

  Lab5_8 lab5_8_1 (
    .in_1(in_1), .in_2(in_2), .in_3(in_3), .in_4(in_4), .in_5(in_5), .in_6(in_6), .in_7(in_7), .in_8(in_8),
    .SSS(in_11), .out_10(out_34), .out_11(out_35), .out_12(out_36), .out_13(out_37), .Cout(lab5_8_1_cout));
  Lab5_8 lab5_8_2 (
    .in_1(in_9), .in_2(in_10), .in_3(in_12), .in_4(in_13), .in_5(in_14), .in_6(in_15), .in_7(in_16),
    .in_8(in_17), .SSS(lab5_8_1_cout), .out_10(out_38), .out_11(out_40), .out_12(out_39), .out_13(out_41),
    .Cout(lab5_8_2_cout));
  Lab5_8 lab5_8_3 (
    .in_1(in_18), .in_2(in_19), .in_3(in_20), .in_4(in_21), .in_5(in_22), .in_6(in_23), .in_7(in_24),
    .in_8(in_26), .SSS(lab5_8_2_cout), .out_10(out_42), .out_11(out_44), .out_12(out_43), .out_13(out_45),
    .Cout(lab5_8_3_cout));
  Lab5_8 lab5_8_4 (
    .in_1(in_25), .in_2(in_27), .in_3(in_28), .in_4(in_29), .in_5(in_30), .in_6(in_31), .in_7(in_32),
    .in_8(in_33), .SSS(lab5_8_3_cout), .out_10(out_47), .out_11(out_46), .out_12(out_50), .out_13(out_48),
    .Cout(out_49));
endmodule

module Lab5_10 (
  input  in_1,
  input  in_2,
  input  in_3,
  input  in_4,
  output out_5,
  output out_6,
  output out_7,
  output out_8,
  output out_9
);

  wire not_1_out, not_2_out;

  not not_1 (not_1_out, 1'b1);
  not not_2 (not_2_out, 1'b1);
  Lab5_5 lab5_5_1 (
    .a0(in_1), .b0(1'b1), .a1(in_2), .b1(1'b1), .a2(in_3), .b2(not_1_out), .a3(in_4), .b3(not_2_out),
    .s0(out_5), .s1(out_6), .s2(out_7), .s3(out_8), .cout(out_9));
endmodule

module Lab5_11 (
  input  in_1,
  input  in_2,
  input  in_3,
  input  in_4,
  input  in_5,
  input  in_6,
  input  in_7,
  input  in_8,
  input  in_9,
  output out_10,
  output out_11,
  output out_12,
  output out_13,
  output out_14
);

  wire lab5_8_1_cout, lab5_8_1_out_10, lab5_8_1_out_11, lab5_8_1_out_12, lab5_8_1_out_13, lab5_10_1_out_9;

  Lab5_8 lab5_8_1 (
    .in_1(in_1), .in_2(in_2), .in_3(in_3), .in_4(in_4), .in_5(in_5), .in_6(in_6), .in_7(in_7), .in_8(in_8),
    .SSS(in_9), .out_10(lab5_8_1_out_10), .out_11(lab5_8_1_out_11), .out_12(lab5_8_1_out_12),
    .out_13(lab5_8_1_out_13), .Cout(lab5_8_1_cout));
  Lab5_10 lab5_10_1 (
    .in_1(lab5_8_1_out_10), .in_2(lab5_8_1_out_11), .in_3(lab5_8_1_out_12), .in_4(lab5_8_1_out_13),
    .out_5(out_10), .out_6(out_11), .out_7(out_12), .out_8(out_13), .out_9(lab5_10_1_out_9));
  or or_1 (out_14, lab5_10_1_out_9, lab5_8_1_cout);
endmodule
