// Logisim project exampra.circ as structural Verilog
module half_adder (
  input  x,
  input  y,
  output s,
  output c
);

  xor xor_1 (s, x, y);
  and and_1 (c, x, y);
endmodule

module full_adder (
  input  x,
  input  y,
  input  cin,
  output s,
  output cout
);

  wire half_adder_1_c, half_adder_1_s, half_adder_2_c;

  half_adder half_adder_1 (.x(x), .y(y), .s(half_adder_1_s), .c(half_adder_1_c));
  half_adder half_adder_2 (.x(half_adder_1_s), .y(cin), .s(s), .c(half_adder_2_c));
  or or_1 (cout, half_adder_2_c, half_adder_1_c);
endmodule

module _4_bit_adder (
  input  a0,
  input  b0,
  input  a1,
  input  b1,
  input  a2,
  input  b2,
  input  a3,
  input  b3,
  input  cin,
  output cout,
  output s0,
  output s1,
  output s2,
  output s3
);

  wire full_adder_1_cout, full_adder_2_cout, full_adder_3_cout;

  full_adder full_adder_1 (.x(a0), .y(b0), .cin(cin), .s(s0), .cout(full_adder_1_cout));
  full_adder full_adder_2 (.x(a1), .y(b1), .cin(full_adder_1_cout), .s(s1), .cout(full_adder_2_cout));
  full_adder full_adder_3 (.x(a2), .y(b2), .cin(full_adder_2_cout), .s(s2), .cout(full_adder_3_cout));
  full_adder full_adder_4 (.x(a3), .y(b3), .cin(full_adder_3_cout), .s(s3), .cout(cout));
endmodule

module _4_bit_add_and_sub (
  input  a0,
  input  a1,
  input  a2,
  input  a3,
  input  b0,
  input  b1,
  input  b2,
  input  b3,
  input  in_9,
  output out_10,
  output out_11,
  output out_12,
  output out_13
);

  wire n4_bit_adder_1_cout, xor_1_out, xor_2_out, xor_3_out, xor_4_out;

  xor xor_1 (xor_1_out, in_9, b0);
  _4_bit_adder u_4_bit_adder_1 (
    .cin(in_9), .a0(a0), .b0(xor_1_out), .a1(a1), .b1(xor_2_out), .a2(a2), .b2(xor_3_out), .a3(a3),
    .b3(xor_4_out), .s0(out_10), .s1(out_11), .s2(out_12), .s3(out_13), .cout(n4_bit_adder_1_cout));
  xor xor_2 (xor_2_out, in_9, b1);
  xor xor_3 (xor_3_out, in_9, b2);
  xor xor_4 (xor_4_out, in_9, b3);
endmodule

module _1digit_bcd_adder (
  input  a0,
  input  b0,
  input  a1,
  input  b1,
  input  a2,
  input  b2,
  input  a3,
  input  b3,
  input  cin,
  output cout,
  output s0,
  output s1,
  output s2,
  output s3
);

  wire and_1_out, and_2_out, n4_bit_adder_1_cout, n4_bit_adder_1_s0, n4_bit_adder_1_s1, n4_bit_adder_1_s2,
       n4_bit_adder_1_s3, n4_bit_adder_2_cout;

  _4_bit_adder u_4_bit_adder_1 (
    .cin(cin), .a0(a0), .b0(b0), .a1(a1), .b1(b1), .a2(a2), .b2(b2), .a3(a3), .b3(b3),
    .s0(n4_bit_adder_1_s0), .s1(n4_bit_adder_1_s1), .s2(n4_bit_adder_1_s2), .s3(n4_bit_adder_1_s3),
    .cout(n4_bit_adder_1_cout));
  _4_bit_adder u_4_bit_adder_2 (
    .cin(1'b0), .a0(n4_bit_adder_1_s0), .b0(1'b0), .a1(n4_bit_adder_1_s1), .b1(cout), .a2(n4_bit_adder_1_s2),
    .b2(cout), .a3(n4_bit_adder_1_s3), .b3(1'b0), .s0(s0), .s1(s1), .s2(s2), .s3(s3),
    .cout(n4_bit_adder_2_cout));
  and and_1 (and_1_out, n4_bit_adder_1_s3, n4_bit_adder_1_s2);
  and and_2 (and_2_out, n4_bit_adder_1_s3, n4_bit_adder_1_s1);
  or or_1 (cout, and_1_out, n4_bit_adder_1_cout, and_2_out);
endmodule

module _4_digit_bcd_adder (
  input  in_1,
  input  in_2,
  input  in_3,
  input  in_4,
  input  in_5,
  input  in_6,
  input  in_7,
  input  in_8,
  input  in_9,
  input  in_10,
  input  in_11,
  input  in_12,
  input  in_13,
  input  in_14,
  input  in_15,
  input  in_16,
  input  in_17,
  input  in_18,
  input  in_19,
  input  in_20,
  input  in_21,
  input  in_22,
  input  in_23,
  input  in_24,
  input  in_25,
  input  in_26,
  input  in_27,
  input  in_28,
  input  in_29,
  input  in_30,
  input  in_31,
  input  in_32,
  input  cin,
  output out_34,
  output out_35,
  output out_36,
  output out_37,
  output out_38,
  output out_39,
  output out_40,
  output out_41,
  output out_42,
  output out_43,
  output out_44,
  output out_45,
  output out_46,
  output out_47,
  output out_48,
  output out_49,
  output out_50
);

  wire n1digit_bcd_adder_1_cout, n1digit_bcd_adder_2_cout, n1digit_bcd_adder_3_cout;

  _1digit_bcd_adder u_1digit_bcd_adder_1 (
    .cin(cin), .a0(in_17), .b0(in_18), .a1(in_19), .b1(in_20), .a2(in_21), .b2(in_22), .a3(in_23),
    .b3(in_24), .s0(out_35), .s1(out_36), .s2(out_37), .s3(out_38), .cout(n1digit_bcd_adder_1_cout));
  _1digit_bcd_adder u_1digit_bcd_adder_2 (
    .cin(n1digit_bcd_adder_1_cout), .a0(in_9), .b0(in_10), .a1(in_11), .b1(in_12), .a2(in_13), .b2(in_14),
    .a3(in_15), .b3(in_16), .s0(out_39), .s1(out_40), .s2(out_41), .s3(out_42),
    .cout(n1digit_bcd_adder_2_cout));
  _1digit_bcd_adder u_1digit_bcd_adder_3 (
    .cin(n1digit_bcd_adder_2_cout), .a0(in_25), .b0(in_26), .a1(in_27), .b1(in_28), .a2(in_29), .b2(in_30),
    .a3(in_31), .b3(in_32), .s0(out_43), .s1(out_44), .s2(out_45), .s3(out_46),
    .cout(n1digit_bcd_adder_3_cout));
  _1digit_bcd_adder u_1digit_bcd_adder_4 (
    .cin(n1digit_bcd_adder_3_cout), .a0(in_1), .b0(in_2), .a1(in_3), .b1(in_4), .a2(in_5), .b2(in_6),
    .a3(in_7), .b3(in_8), .s0(out_47), .s1(out_48), .s2(out_49), .s3(out_50), .cout(out_34));
endmodule

module _4bit_bcd_to_ex3 (
  input  a0,
  input  a1,
  input  a2,
  input  a3,
  input  in_5
);

  _4_bit_adder u_4_bit_adder_1 (
    .cin(in_5), .a0(a0), .b0(1'b1), .a1(a1), .b1(1'b1), .a2(a2), .b2(1'b0), .a3(a3), .b3(1'b0));  // open: s0, s1, s2, s3, cout
endmodule

module excess3_adder (
  input  in_1,
  input  in_2,
  input  in_3,
  input  in_4,
  input  in_5,
  input  in_6,
  input  in_7,
  input  in_8,
  input  in_9,
  input  in_10,
  input  in_11,
  input  in_12,
  output out_13,
  output out_14,
  output out_15,
  output out_16,
  output out_17
);

  wire and_1_out, and_2_out, and_3_out, and_4_out, and_5_out, and_6_out, and_7_out, and_8_out,
       n4_bit_adder_1_s0, n4_bit_adder_1_s1, n4_bit_adder_1_s2, n4_bit_adder_1_s3, n4_bit_adder_2_s0,
       n4_bit_adder_2_s1, n4_bit_adder_2_s2, n4_bit_adder_2_s3, n4_bit_adder_3_s0, n4_bit_adder_3_s1,
       n4_bit_adder_3_s2, n4_bit_adder_3_s3, not_1_out, not_2_out, or_1_out, or_2_out, or_3_out, or_4_out;

  _4_bit_adder u_4_bit_adder_1 (
    .cin(in_9), .a0(in_1), .b0(1'b1), .a1(in_2), .b1(1'b1), .a2(in_3), .b2(1'b0), .a3(in_4), .b3(1'b0),
    .s0(n4_bit_adder_1_s0), .s1(n4_bit_adder_1_s1), .s2(n4_bit_adder_1_s2), .s3(n4_bit_adder_1_s3));  // open: cout
  _4_bit_adder u_4_bit_adder_2 (
    .cin(in_11), .a0(n4_bit_adder_1_s0), .b0(n4_bit_adder_3_s0), .a1(n4_bit_adder_1_s1),
    .b1(n4_bit_adder_3_s1), .a2(n4_bit_adder_1_s2), .b2(n4_bit_adder_3_s2), .a3(n4_bit_adder_1_s3),
    .b3(n4_bit_adder_3_s3), .s0(n4_bit_adder_2_s0), .s1(n4_bit_adder_2_s1), .s2(n4_bit_adder_2_s2),
    .s3(n4_bit_adder_2_s3), .cout(out_13));
  _4_bit_adder u_4_bit_adder_3 (
    .cin(in_10), .a0(in_5), .b0(1'b1), .a1(in_6), .b1(1'b1), .a2(in_7), .b2(1'b0), .a3(in_8), .b3(1'b0),
    .s0(n4_bit_adder_3_s0), .s1(n4_bit_adder_3_s1), .s2(n4_bit_adder_3_s2), .s3(n4_bit_adder_3_s3));  // open: cout
  not not_1 (not_1_out, out_13);
  _4_bit_adder u_4_bit_adder_4 (
    .cin(in_12), .a0(n4_bit_adder_2_s0), .b0(or_1_out), .a1(n4_bit_adder_2_s1), .b1(or_2_out),
    .a2(n4_bit_adder_2_s2), .b2(or_3_out), .a3(n4_bit_adder_2_s3), .b3(or_4_out), .s0(out_14), .s1(out_15),
    .s2(out_16), .s3(out_17));  // open: cout
  and and_1 (and_1_out, not_1_out, 1'b0);
  and and_2 (and_2_out, not_1_out, 1'b1);
  and and_3 (and_3_out, not_1_out, 1'b1);
  or or_1 (or_1_out, and_2_out, and_5_out);
  and and_4 (and_4_out, not_1_out, 1'b1);
  or or_2 (or_2_out, and_1_out, and_6_out);
  not not_2 (not_2_out, not_1_out);
  or or_3 (or_3_out, and_3_out, and_7_out);
  and and_5 (and_5_out, not_2_out, 1'b1);
  and and_6 (and_6_out, not_2_out, 1'b1);
  or or_4 (or_4_out, and_4_out, and_8_out);
  and and_7 (and_7_out, not_2_out, 1'b0);
  and and_8 (and_8_out, not_2_out, 1'b0);
endmodule
