// Logisim project try.circ as structural Verilog: 5 circuits, main circuit main
module main (
  input  x,
  input  y,
  output s,
  output c
);

  xor xor_1 (s, x, y);
  and and_1 (c, x, y);
endmodule

// Cout
module Full_adder (
  input  Cin,
  input  x,
  input  y,
  output s,
  output Cout
);

  wire main_1_c, main_1_s, main_2_c;

  main main_1 (.x(x), .y(y), .s(main_1_s), .c(main_1_c));
  main main_2 (.x(main_1_s), .y(Cin), .s(s), .c(main_2_c));
  or or_1 (Cout, main_2_c, main_1_c);
endmodule

module _4_bit_adder (
  input  b3,
  input  b2,
  input  b1,
  input  b0,
  input  a3,
  input  a2,
  input  a1,
  input  a0,
  input  Cin,
  output Cout,
  output s3,
  output s2,
  output s1,
  output s0
);

  wire full_adder_1_cout, full_adder_2_cout, full_adder_3_cout;

  Full_adder full_adder_1 (.Cin(Cin), .x(a0), .y(b0), .s(s0), .Cout(full_adder_1_cout));
  Full_adder full_adder_2 (.Cin(full_adder_1_cout), .x(a1), .y(b1), .s(s1), .Cout(full_adder_2_cout));
  Full_adder full_adder_3 (.Cin(full_adder_2_cout), .x(a2), .y(b2), .s(s2), .Cout(full_adder_3_cout));
  Full_adder full_adder_4 (.Cin(full_adder_3_cout), .x(a3), .y(b3), .s(s3), .Cout(Cout));
endmodule

module _4_bit_adder_subtractor (
  input  b3,
  input  b2,
  input  b1,
  input  b0,
  input  a3,
  input  a2,
  input  a1,
  input  a0,
  input  control_input,
  output Cout,
  output s3,
  output s2,
  output s1,
  output s0
);

  wire xor_1_out, xor_2_out, xor_3_out, xor_4_out;

  xor xor_1 (xor_1_out, control_input, b0);
  xor xor_2 (xor_2_out, control_input, b1);
  xor xor_3 (xor_3_out, control_input, b2);
  xor xor_4 (xor_4_out, control_input, b3);
  _4_bit_adder u_4_bit_adder_1 (
    .Cin(control_input), .b3(xor_4_out), .b2(xor_3_out), .b1(xor_2_out), .b0(xor_1_out), .a3(a3), .a2(a2),
    .a1(a1), .a0(a0), .s3(s3), .s2(s2), .s1(s1), .s0(s0), .Cout(Cout));
endmodule

module _12_bit_adder_subtractor (
  input  b3,
  input  b2,
  input  b1,
  input  b0,
  input  b7,
  input  b6,
  input  b5,
  input  b4,
  input  b11,
  input  b10,
  input  b9,
  input  b8,
  input  control_input,
  input  in_14,
  input  in_15,
  input  in_16,
  input  in_17,
  input  in_18,
  input  in_19,
  input  in_20,
  input  in_21,
  input  in_22,
  input  in_23,
  input  in_24,
  input  in_25,
  output out,
  output out_27,
  output out_28,
  output out_29,
  output out_30,
  output out_31,
  output out_32,
  output out_33,
  output out_34,
  output out_35,
  output out_36,
  output out_37,
  output out_38
);

  wire n4_bit_adder_subtractor_1_cout, n4_bit_adder_subtractor_2_cout;

  _4_bit_adder_subtractor u_4_bit_adder_subtractor_1 (
    .control_input(control_input), .b3(b3), .b2(b2), .b1(b1), .b0(b0), .a3(in_14), .a2(in_15), .a1(in_16),
    .a0(in_17), .s3(out_27), .s2(out_28), .s1(out_29), .s0(out_30), .Cout(n4_bit_adder_subtractor_1_cout));
  _4_bit_adder_subtractor u_4_bit_adder_subtractor_2 (
    .control_input(n4_bit_adder_subtractor_1_cout), .b3(b7), .b2(b6), .b1(b5), .b0(b4), .a3(in_18),
    .a2(in_19), .a1(in_20), .a0(in_21), .s3(out_31), .s2(out_32), .s1(out_33), .s0(out_34),
    .Cout(n4_bit_adder_subtractor_2_cout));
  _4_bit_adder_subtractor u_4_bit_adder_subtractor_3 (
    .control_input(n4_bit_adder_subtractor_2_cout), .b3(b11), .b2(b10), .b1(b9), .b0(b8), .a3(in_22),
    .a2(in_23), .a1(in_24), .a0(in_25), .s3(out_35), .s2(out_36), .s1(out_37), .s0(out_38), .Cout(out));
endmodule
